# Fritzing sketch ESP8266_Sketch (saved by Fritzing 0.9.6b)
breadboards: 1

parts:
  Gizwits_WiFi_Witty_ESP-12F1 = Gizwits WiFi Witty ESP-12F
  Part1 = Arduino Ethernet Shield (Rev3)
  LED1 = LED - 3mm [color="Red (633nm)" current=0.030 package="3 mm [THT]"]
  R1 = Resistor [tolerance=±5% resistance=220 package="0402 [SMD]"]
  S1 = SWITCH-MOMENTARY-2 [package=tactile-pth]
  S2 = Toggle Switch [package=THT]

nets:
  N1: Gizwits_WiFi_Witty_ESP-12F1.REST, S1.2
  VCC: Gizwits_WiFi_Witty_ESP-12F1.CH_PD, Gizwits_WiFi_Witty_ESP-12F1.VCC, Part1.3V3
  GND: Gizwits_WiFi_Witty_ESP-12F1.GND, Gizwits_WiFi_Witty_ESP-12F1.GPIO15, Part1.GND, R1.Pin_0, S1.1, S2.L2
  N2: Gizwits_WiFi_Witty_ESP-12F1.GPIO0, S2.COM
  N3: Gizwits_WiFi_Witty_ESP-12F1.GPIO4, LED1.anode
  N4: Gizwits_WiFi_Witty_ESP-12F1.RXD, Part1.RX/D0
  N5: Gizwits_WiFi_Witty_ESP-12F1.TXD, Part1.TX/D1
  N6: LED1.cathode, R1.Pin_1
